# Fritzing sketch flipper32 (saved by Fritzing 0.9.10b)
breadboards: 2

parts:
  U1 = ESP32-38PinWide [part_number=ESP32-38PinWide]
  IR1 = TSOP312.., 314.. [package=THT]
  LED1 = LEDs [package=led10mm]
  Componente1 = PN532 Elechouse RFID NFC Module V3
  SD_card_module1 = SD Card Module
  R1 = Resistor [tolerance=±5% resistance=150 package="0603 [SMD]"]
  R2 = Resistor [tolerance=±5% resistance=100 package="0603 [SMD]"]

nets:
  N1: U1.GPIO35, IR1.GND
  N2: U1.GPIO32, LED1.A
  GND: U1.GPIO11, Componente1.GND, SD_card_module1.GND, R1.Pin_1
  VIN: U1.VIN, Componente1.VCC, SD_card_module1.+5, R2.Pin_1
  N3: U1.GPIO5, SD_card_module1.CS
  N4: U1.GPIO18, SD_card_module1.SCK
  N5: U1.GPIO19, SD_card_module1.MISO
  N6: U1.GPIO21, Componente1.SDA
  N7: U1.GPIO22, Componente1.SCL
  N8: U1.GPIO23, SD_card_module1.MOSI
  N9: IR1.Data, R2.Pin_0
  N10: LED1.C, R1.Pin_0

custom parts:
  ESP32-38PinWide: Generic 38-Pin ESP32 with wide format (only access to one side of pins on a breadboard) based on Stephen Lilley's HiLetgo ESP-WROOM-32 ESP32 ESP-32S Development Board.
  PN532 Elechouse RFID NFC Module V3: NFC is a popular technology in recent years. We often heard this work while smart phone company such as Samsung or HTC introduces their latest high-end phones. Almost all the high-end phone in the market support NFC. Near field communication (NFC) is a set of standards for smart phones and similar devices to establish radio communication with each other by touching them together or bringing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
  SD Card Module: SD Card Module Slot Socket Reader For Arduino ARM MCU
